# Fritzing sketch portail_master_0 (saved by Fritzing 0.9.9b)
circuit board: 5.45782cm x 5.8532cm
breadboards: 1

parts:
  Composant2 = Arduino Nano (Rev3.0)
  J5 = Screw terminal - 2 pins [part_number=ALIM12V package=THT]
  R11 = Resistor [tolerance=±5% power=0.25 resistance=1k package=THT]
  M3 = DC Motor
  S3 = H-Bridge with L298N [part_number=ln298]
  U7 = FS1000A - 433Mhz RF Transmitter [package=THT]
  C18 = Ceramic Capacitor [capacitance="100 nF" voltage=35V package="0805 [SMD, multilayer]"]
  C19 = Ceramic Capacitor [capacitance=22pF voltage=35V package="0805 [SMD, multilayer]"]
  ANT1 = Antenna
  S6 = Pushbutton [part_number=TRIG package=THT]
  S9 = Pushbutton [part_number=ROT package=THT]
  S5 = SWITCH-MOMENTARY-2 [part_number=POC package=reed_switch_pth]
  C26 = Electrolytic Capacitor [capacitance=0.1mF voltage=35V package="100 mil [THT, electrolytic]"]
  C28 = Electrolytic Capacitor [capacitance=0.1mF voltage=35V package="100 mil [THT, electrolytic]"]
  U8 = L200 [package="pentawatt h"]
  C29 = Ceramic Capacitor [capacitance="100 nF" voltage=35V package="0805 [SMD, multilayer]"]
  VR1 = Trimpot-3296 [part_number=22k package=3386u]
  R20 = Resistor [tolerance=±5% power=0.25 resistance=10k package=THT]
  RHT3 = Humidity and Temperature Sensor RHT03 [part_number=DHT22]
  C30 = Electrolytic Capacitor [capacitance=1mF voltage=35V package="100 mil [THT, electrolytic]"]
  R21 = Resistor [tolerance=±5% power=0.25 resistance=4.7k package=THT]
  C31 = Electrolytic Capacitor [capacitance=10µF voltage=35V package="100 mil [THT, electrolytic]"]

nets:
  GND: Composant2.GND, J5.pin1, S3.GND, U7.GND, C18.1, C19.1, S6.leg0, S9.leg1, C26.-, C28.-, U8.GND, U8.REF, C29.1, VR1.CW, RHT3.GND_2, C30.-, R21.Pin_1, C31.-
  N1: Composant2.D2, S9.leg0
  N2: Composant2.D3, R11.Pin_1, S6.leg1, C31.+
  N3: Composant2.D4, RHT3.Data-signal
  N4: Composant2.D5, S3.ENA, S3.ENB
  N5: Composant2.D6, S3.IN2
  N6: Composant2.D7, S3.IN1, S3.IN4
  N7: Composant2.D8, S5.2
  N8: Composant2.D12/MISO, U7.DATA
  VIN: Composant2.VIN, J5.pin2, U7.VCC, C26.+, U8.INPUT
  5V: Composant2.5V, R11.Pin_0, C18.0, C19.0, C28.+, VR1.CCW, RHT3.Vcc
  N9: Composant2.A7, R20.Pin_1, R21.Pin_0
  N10: Composant2.A6, VR1.WIPER
  N11: M3.pin_1, S3.M1-02, S3.M2-01
  N12: M3.pin_2, S3.M1-01, S3.M2-02
  N13: S3.12V, U8.LIMIT, U8.OUTPUT, C29.0, R20.Pin_0, C30.+
  N14: U7.Antenna, ANT1.antenna_lead

custom parts:
  H-Bridge with L298N: h-bridge
  FS1000A - 433Mhz RF Transmitter: This is 433Mhz RF transmitter with receiver kit for Arduino ARM MCU wireless Application environment: Remote control switch, receiver module, motorcycles, automobile anti-theft products, home security products, electric doors, shutter doors, windows, remote control socket, remote control LED, remote audio remote control electric doors, garage door remote control, remote control retractable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
  L200: ADJUSTABLE VOLTAGE AND CURRENT REGULATOR
  Trimpot-3296: Trimpot 3296 / 25 turn stand
