# Fritzing sketch portail_master_0_old (saved by Fritzing 0.9.9b)
circuit board: 5.45782cm x 5.8532cm
breadboards: 1

parts:
  Composant2 = Arduino Nano (Rev3.0)
  J5 = Screw terminal - 2 pins [part_number=ALIM12V package=THT]
  R11 = Resistor [tolerance=±5% power=0.25 resistance=1k package=THT]
  R12 = Resistor [tolerance=±5% power=0.25 resistance=1k package=THT]
  R14 = Resistor [tolerance=±5% power=0.25 resistance=10k package=THT]
  LCD3 = LCD screen [part_number=1602A]
  LCM1602_IIC3 = LCM1602 IIC [part_number="LCM1602 IIC" chip_label="LCM1602 IIC" package="DIP (Dual Inline) [THT]"]
  M3 = DC Motor
  S3 = H-Bridge with L298N [part_number=ln298]
  U7 = FS1000A - 433Mhz RF Transmitter [package=THT]
  C18 = Ceramic Capacitor [capacitance="100 nF" voltage=35V package="0805 [SMD, multilayer]"]
  C19 = Ceramic Capacitor [capacitance=22pF voltage=35V package="0805 [SMD, multilayer]"]
  ANT1 = Antenna
  S6 = Pushbutton [part_number=TRIG package=THT]
  S9 = Pushbutton [part_number=ROT package=THT]
  S5 = SWITCH-MOMENTARY-2 [part_number=POC package=reed_switch_pth]
  R15 = Resistor [tolerance=±5% power=0.25 resistance=10k package=THT]
  R16 = Resistor [tolerance=±5% power=0.25 resistance=10k package=THT]
  R17 = Resistor [tolerance=±5% power=2W resistance=1 package=THT]
  C26 = Electrolytic Capacitor [capacitance=0.1mF voltage=35V package="100 mil [THT, electrolytic]"]
  C27 = Electrolytic Capacitor [capacitance=10µF voltage=35V package="100 mil [THT, electrolytic]"]
  R19 = Resistor [tolerance=±5% power=0.25 resistance=1k package=THT]
  C28 = Electrolytic Capacitor [capacitance=0.1mF voltage=35V package="100 mil [THT, electrolytic]"]

nets:
  GND: Composant2.GND, J5.pin1, LCM1602_IIC3.GND, U7.GND, C18.1, C19.1, S6.leg0, S9.leg1, S5.1, R17.Pin_1, C26.-, C27.-, C28.-
  N1: Composant2.D2, R12.Pin_1, S9.leg0
  N2: Composant2.D3, R11.Pin_1, S6.leg1
  N3: Composant2.D8, S5.2
  N4: Composant2.D12/MISO, U7.DATA
  VIN: Composant2.VIN, J5.pin2, S3.12V, C26.+
  VCC: Composant2.5V, R11.Pin_0, R12.Pin_0, LCM1602_IIC3.VCC, U7.VCC, C18.0, C19.0, C28.+
  N5: Composant2.A7, R19.Pin_1
  N6: Composant2.A5, LCM1602_IIC3.SCL
  N7: Composant2.A4, LCM1602_IIC3.SDA
  N8: R14.Pin_0, S3.ENA, S3.ENB
  VSS: LCD3.VSS, LCM1602_IIC3.VSS
  VDD: LCD3.VDD, LCM1602_IIC3.VDD
  N9: LCD3.V0, LCM1602_IIC3.V0
  N10: LCD3.RS, LCM1602_IIC3.RS
  N11: LCD3.R/W, LCM1602_IIC3.RW
  N12: LCD3.E, LCM1602_IIC3.E
  N13: LCD3.DB0, LCM1602_IIC3.D0
  N14: LCD3.DB1, LCM1602_IIC3.D1
  N15: LCD3.DB2, LCM1602_IIC3.D2
  N16: LCD3.DB3, LCM1602_IIC3.D3
  N17: LCD3.DB4, LCM1602_IIC3.D4
  N18: LCD3.DB5, LCM1602_IIC3.D5
  N19: LCD3.DB6, LCM1602_IIC3.D6
  N20: LCD3.DB7, LCM1602_IIC3.D7
  N21: LCD3.LED+, LCM1602_IIC3.A
  N22: LCD3.LED-, LCM1602_IIC3.K
  N23: LCM1602_IIC3.LED_A, LCM1602_IIC3.LED_B
  N24: M3.pin_1, S3.M1-02, S3.M2-01
  N25: M3.pin_2, S3.M1-01, S3.M2-02
  N26: S3.GND, R17.Pin_0, C27.+, R19.Pin_0
  N27: S3.IN1, S3.IN3, R15.Pin_0
  N28: S3.IN2, S3.IN4, R16.Pin_0
  N29: U7.Antenna, ANT1.antenna_lead

custom parts:
  LCM1602 IIC: I2C-Module to use a 1602 or 2004 LCD on with the wire.h libory Serial LCD Modul
  H-Bridge with L298N: h-bridge
  FS1000A - 433Mhz RF Transmitter: This is 433Mhz RF transmitter with receiver kit for Arduino ARM MCU wireless Application environment: Remote control switch, receiver module, motorcycles, automobile anti-theft products, home security products, electric doors, shutter doors, windows, remote control socket, remote control LED, remote audio remote control electric doors, garage door remote control, remote control retractable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
