# Fritzing sketch portail_na_1 (saved by Fritzing 0.9.9b)
circuit board: 5.45782cm x 5.8532cm
breadboards: 1

parts:
  Composant2 = Arduino Nano (Rev3.0)
  J5 = Screw terminal - 2 pins [part_number=ALIM12V package=THT]
  C10 = Electrolytic Capacitor [capacitance=0.1mF voltage=35V package="1010 [SMD, electrolytic]"]
  C12 = Ceramic Capacitor [capacitance=0.22mF voltage=35V package="0805 [SMD, multilayer]"]
  C13 = Ceramic Capacitor [capacitance="100 nF" voltage=35V package="0805 [SMD, multilayer]"]
  J10 = Screw terminal - 2 pins [part_number=TRIG package=THT]
  J11 = Screw terminal - 2 pins [package=THT]
  J12 = Screw terminal - 2 pins [package=THT]
  J13 = Screw terminal - 2 pins [part_number=ROT package=THT]
  J14 = screw terminal, 2 pins [part_number=MOTOR]
  U6 = L200 [package="pentawatt h"]
  C16 = Capacitor Polarized [package=cpol-radial-10uf-25v]
  C17 = Capacitor Polarized [package=cpol-radial-10uf-25v]
  R11 = Resistor [tolerance=±5% power=0.25 resistance=1k package=THT]
  R12 = Resistor [tolerance=±5% power=0.25 resistance=1k package=THT]
  R13 = Resistor [tolerance=±5% power=0.25 resistance=1k package=THT]
  R14 = Resistor [tolerance=±5% power=0.25 resistance=100k package=THT]
  R15 = Resistor [tolerance=±5% power=0.25 resistance=680 package=THT]
  LCD3 = LCD screen [part_number=1602A]
  LCM1602_IIC3 = LCM1602 IIC [part_number="LCM1602 IIC" chip_label="LCM1602 IIC" package="DIP (Dual Inline) [THT]"]
  M3 = DC Motor
  S3 = H-Bridge with L298N [part_number=ln298]

nets:
  GND: Composant2.GND, J5.pin1, C10.-, C12.0, C13.1, J10.pin2, J13.pin2, J14.pin1, U6.GND, U6.REF, C16.-, C17.-, R15.Pin_0, LCM1602_IIC3.GND, S3.GND
  N1: Composant2.D2, J13.pin1, R12.Pin_1
  N2: Composant2.D3, J10.pin1, R11.Pin_1
  N3: Composant2.D5, J12.pin1, S3.ENA, S3.ENB
  N4: Composant2.D6, J12.pin2, S3.IN1, S3.IN3
  N5: Composant2.D7, J11.pin1, S3.IN2, S3.IN4
  N6: Composant2.D8, J11.pin2
  N7: Composant2.VIN, J5.pin2, C10.+, C12.1, U6.INPUT
  5V: Composant2.5V, C17.+, R11.Pin_0, R12.Pin_0, LCM1602_IIC3.VCC
  N8: Composant2.A7, R14.Pin_1
  N9: Composant2.A5, LCM1602_IIC3.SCL
  N10: Composant2.A4, LCM1602_IIC3.SDA
  N11: C13.0, J14.pin2, U6.LIMIT, U6.OUTPUT, R13.Pin_1, S3.12V
  N12: C16.+, R13.Pin_0, R14.Pin_0, R15.Pin_1
  VSS: LCD3.VSS, LCM1602_IIC3.VSS
  VDD: LCD3.VDD, LCM1602_IIC3.VDD
  N13: LCD3.V0, LCM1602_IIC3.V0
  N14: LCD3.RS, LCM1602_IIC3.RS
  N15: LCD3.R/W, LCM1602_IIC3.RW
  N16: LCD3.E, LCM1602_IIC3.E
  N17: LCD3.DB0, LCM1602_IIC3.D0
  N18: LCD3.DB1, LCM1602_IIC3.D1
  N19: LCD3.DB2, LCM1602_IIC3.D2
  N20: LCD3.DB3, LCM1602_IIC3.D3
  N21: LCD3.DB4, LCM1602_IIC3.D4
  N22: LCD3.DB5, LCM1602_IIC3.D5
  N23: LCD3.DB6, LCM1602_IIC3.D6
  N24: LCD3.DB7, LCM1602_IIC3.D7
  N25: LCD3.LED+, LCM1602_IIC3.A
  N26: LCD3.LED-, LCM1602_IIC3.K
  N27: LCM1602_IIC3.LED_A, LCM1602_IIC3.LED_B
  N28: M3.pin_1, S3.M1-02, S3.M2-01
  N29: M3.pin_2, S3.M1-01, S3.M2-02

custom parts:
  L200: ADJUSTABLE VOLTAGE AND CURRENT REGULATOR
  LCM1602 IIC: I2C-Module to use a 1602 or 2004 LCD on with the wire.h libory Serial LCD Modul
  H-Bridge with L298N: h-bridge
