# Fritzing sketch portail_slave_1 (saved by Fritzing 0.9.9b)
circuit board: 5.45782cm x 5.8532cm
breadboards: 1

parts:
  Composant2 = Arduino Nano (Rev3.0)
  J5 = Screw terminal - 2 pins [part_number=ALIM12V package=THT]
  R11 = Resistor [tolerance=±5% power=0.25 resistance=1k package=THT]
  M3 = DC Motor
  S3 = H-Bridge with L298N [part_number=ln298]
  C18 = Ceramic Capacitor [capacitance="100 nF" voltage=35V package="0805 [SMD, multilayer]"]
  C19 = Ceramic Capacitor [capacitance=22pF voltage=35V package="0805 [SMD, multilayer]"]
  ANT1 = Antenna
  S6 = Pushbutton [part_number=TRIG package=THT]
  S9 = Pushbutton [part_number=ROT package=THT]
  C26 = Electrolytic Capacitor [capacitance=0.1mF voltage=35V package="100 mil [THT, electrolytic]"]
  U8 = L200 [package="pentawatt h"]
  C29 = Ceramic Capacitor [capacitance="100 nF" voltage=35V package="0805 [SMD, multilayer]"]
  VR1 = Trimpot-3296 [part_number=22k package=3386u]
  R20 = Resistor [tolerance=±5% power=0.25 resistance=10k package=THT]
  C30 = Electrolytic Capacitor [capacitance=1mF voltage=35V package="100 mil [THT, electrolytic]"]
  R21 = Resistor [tolerance=±5% power=0.25 resistance=4.7k package=THT]
  U9 = XD-RF-5V [package=THT]
  C28 = Electrolytic Capacitor [capacitance=0.1mF voltage=35V package="100 mil [THT, electrolytic]"]

nets:
  GND: Composant2.GND, J5.pin1, S3.GND, C18.1, C19.1, S6.leg0, S9.leg1, C26.-, U8.GND, U8.REF, C29.1, VR1.CW, C30.-, R21.Pin_1, U9.GND, C28.-
  N1: Composant2.D2, S9.leg0
  N2: Composant2.D3, R11.Pin_1, S6.leg1
  N3: Composant2.D5, S3.ENA, S3.ENB
  N4: Composant2.D6, S3.IN2
  N5: Composant2.D7, S3.IN1, S3.IN4
  N6: Composant2.D11/MOSI, U9.DATA
  N7: Composant2.VIN, J5.pin2, C26.+, U8.INPUT
  5V: Composant2.5V, R11.Pin_0, C18.0, C19.0, VR1.CCW, U9.VCC, C28.+
  N8: Composant2.A7, R20.Pin_1, R21.Pin_0
  N9: Composant2.A6, VR1.WIPER
  N10: M3.pin_1, S3.M1-02, S3.M2-01
  N11: M3.pin_2, S3.M1-01, S3.M2-02
  N12: S3.12V, U8.LIMIT, C29.0, R20.Pin_0, C30.+
  N13: ANT1.antenna_lead, U9.Attenna

custom parts:
  H-Bridge with L298N: h-bridge
  L200: ADJUSTABLE VOLTAGE AND CURRENT REGULATOR
  Trimpot-3296: Trimpot 3296 / 25 turn stand
  XD-RF-5V: This is 433Mhz RF transmitter with receiver kit for Arduino ARM MCU wireless Application environment: Remote control switch, receiver module, motorcycles, automobile anti-theft products, home security products, electric doors, shutter doors, windows, remote control socket, remote control LED, remote audio remote control electric doors, garage door remote control, remote control retractable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
