# Fritzing sketch receiver_7segments (saved by Fritzing 0.9.9b)
breadboards: 2

parts:
  4511 = IC, DIP package, 16 pins [chip_label=4511]  # not connected
  LED2 = LED - 5mm [color="Red (633nm)" current=0.030 package="5 mm [THT]"]  # not connected
  Composant1 = Arduino Nano (Rev3.0)  # not connected
  4511_2 = IC, DIP package, 16 pins [chip_label=4511]  # not connected
  4511_3 = IC, DIP package, 16 pins [chip_label=4511]  # not connected
  SN_1 = SN 74154 [package="DIP24 [THT]"]  # not connected
  7_Segment2 = HDSP3405
  7_Segment6 = HDSP3405
  7_Segment5 = HDSP3405  # not connected

nets:
  N1: 7_Segment2.common_cathode#3, 7_Segment2.common_cathode#5, 7_Segment2.common_cathode#11, 7_Segment2.common_cathode#16
  N2: 7_Segment6.common_cathode#3, 7_Segment6.common_cathode#5, 7_Segment6.common_cathode#11, 7_Segment6.common_cathode#16

custom parts:
  SN 74154: 4 line to 16 line decoders/demultiplexers
  HDSP3405: 7 Segment Display with common cathode.
