# Fritzing sketch portail_board (saved by Fritzing 0.9.9b)
circuit board: 5.45782cm x 5.8532cm
breadboards: 1

parts:
  Composant2 = Arduino Nano (Rev3.0)
  J5 = Screw terminal - 2 pins [part_number=ALIM12V package=THT]
  C10 = Electrolytic Capacitor [capacitance=0.1mF voltage=35V package="1010 [SMD, electrolytic]"]
  C12 = Ceramic Capacitor [capacitance=0.22mF voltage=35V package="0805 [SMD, multilayer]"]
  C13 = Ceramic Capacitor [capacitance="100 nF" voltage=35V package="0805 [SMD, multilayer]"]
  J10 = Screw terminal - 2 pins [part_number=TRIG package=THT]
  J11 = Screw terminal - 2 pins [package=THT]
  J12 = Screw terminal - 2 pins [package=THT]
  J13 = Screw terminal - 2 pins [part_number=ROT package=THT]
  J14 = screw terminal, 2 pins [part_number=MOTOR]
  U6 = L200 [package="pentawatt h"]
  C16 = Capacitor Polarized [package=cpol-radial-10uf-25v]
  C17 = Capacitor Polarized [package=cpol-radial-10uf-25v]
  R11 = Resistor [tolerance=±5% power=0.25 resistance=1k package=THT]
  R12 = Resistor [tolerance=±5% power=0.25 resistance=1k package=THT]
  R13 = Resistor [tolerance=±5% power=0.25 resistance=1k package=THT]
  R14 = Resistor [tolerance=±5% power=0.25 resistance=100k package=THT]
  R15 = Resistor [tolerance=±5% power=0.25 resistance=680 package=THT]

nets:
  GND: Composant2.GND, J5.pin1, C10.-, C12.0, C13.1, J10.pin2, J13.pin2, J14.pin1, U6.GND, U6.REF, C16.-, C17.-, R15.Pin_0
  N1: Composant2.D2, J13.pin1, R12.Pin_1
  N2: Composant2.D3, J10.pin1, R11.Pin_1
  N3: Composant2.D5, J12.pin1
  N4: Composant2.D6, J12.pin2
  N5: Composant2.D7, J11.pin1
  N6: Composant2.D8, J11.pin2
  N7: Composant2.VIN, J5.pin2, C10.+, C12.1, U6.INPUT
  N8: Composant2.5V, C17.+, R11.Pin_0, R12.Pin_0
  N9: Composant2.A7, R14.Pin_1
  N10: C13.0, J14.pin2, U6.LIMIT, U6.OUTPUT, R13.Pin_1
  N11: C16.+, R13.Pin_0, R14.Pin_0, R15.Pin_1

custom parts:
  L200: ADJUSTABLE VOLTAGE AND CURRENT REGULATOR
