# Fritzing sketch portail_na_1 (saved by Fritzing 0.9.9b)
circuit board: 8.46667cm x 5.64444cm
breadboards: 1

parts:
  Composant1 = Arduino Nano (Rev3.0)
  U1 = XD-RF-5V [package=THT]
  U2 = FS1000A - 433Mhz RF Transmitter [package=THT]
  U3 = L200 [package="pentawatt h"]
  J1 = Screw terminal - 2 pins [part_number=ALIM12V package=THT]
  J3 = Screw terminal - 2 pins [part_number=COUNTROT package=THT]
  R1 = Resistor [tolerance=±5% resistance=1k package="2010 [SMD]"]
  R2 = Resistor [tolerance=±5% resistance=680 package="2010 [SMD]"]
  R3 = Resistor [tolerance=±5% resistance=100k package="2010 [SMD]"]
  C2 = Electrolytic Capacitor [capacitance=0.1mF voltage=35V package="1010 [SMD, electrolytic]"]
  C3 = Electrolytic Capacitor [capacitance=4.7µF voltage=35V package="1010 [SMD, electrolytic]"]
  C4 = Ceramic Capacitor [capacitance=0.22mF voltage=35V package="0805 [SMD, multilayer]"]
  C5 = Ceramic Capacitor [capacitance="100 nF" voltage=35V package="0805 [SMD, multilayer]"]
  R4 = Resistor [tolerance=±5% resistance=1k package="2010 [SMD]"]
  R5 = Resistor [tolerance=±5% resistance=1k package="2010 [SMD]"]
  J2 = screw terminal, 2 pins [part_number=TRIG]
  LCD1 = LCD screen [part_number=1602A]
  LCM1602_IIC1 = LCM1602 IIC [part_number="LCM1602 IIC" chip_label="LCM1602 IIC" package="DIP (Dual Inline) [THT]"]
  M1 = DC Motor
  C6 = Electrolytic Capacitor [capacitance=0.1mF voltage=35V package="1010 [SMD, electrolytic]"]
  C7 = Electrolytic Capacitor [capacitance=10µF voltage=35V package="1010 [SMD, electrolytic]"]
  C8 = Ceramic Capacitor [capacitance="100 nF" voltage=35V package="0805 [SMD, multilayer]"]  # not connected
  C9 = Ceramic Capacitor [capacitance=22pF voltage=35V package="0805 [SMD, multilayer]"]  # not connected
  S1 = H-Bridge with L298N [part_number=ln298]

nets:
  GND: Composant1.GND, U1.GND, U2.GND, U3.GND, J1.pin1, J3.pin1, R2.Pin_1, C2.-, C3.-, C4.0, C5.1, J2.pin1, LCM1602_IIC1.GND, C6.-, C7.-, S1.GND
  N1: Composant1.D2, J3.pin2, R4.Pin_0
  N2: Composant1.D3, J2.pin2
  N3: Composant1.D4, R5.Pin_0
  N4: Composant1.D11/MOSI, U1.DATA
  N5: Composant1.D12/MISO, U2.DATA
  VIN: Composant1.VIN, U2.VCC, U3.INPUT, J1.pin2, C2.+, C4.1
  VCC: Composant1.5V, U1.VCC, R4.Pin_1, R5.Pin_1, LCM1602_IIC1.VCC, C6.+
  N6: Composant1.A7, R3.Pin_0
  N7: Composant1.A5, LCM1602_IIC1.SCL
  N8: Composant1.A4, LCM1602_IIC1.SDA
  N9: U3.OUTPUT, R1.Pin_0, S1.12V
  N10: R1.Pin_1, R2.Pin_0, R3.Pin_1, C3.+
  VSS: LCD1.VSS, LCM1602_IIC1.VSS
  VDD: LCD1.VDD, LCM1602_IIC1.VDD
  N11: LCD1.V0, LCM1602_IIC1.V0
  N12: LCD1.RS, LCM1602_IIC1.RS
  N13: LCD1.R/W, LCM1602_IIC1.RW
  N14: LCD1.E, LCM1602_IIC1.E
  N15: LCD1.DB0, LCM1602_IIC1.D0
  N16: LCD1.DB1, LCM1602_IIC1.D1
  N17: LCD1.DB2, LCM1602_IIC1.D2
  N18: LCD1.DB3, LCM1602_IIC1.D3
  N19: LCD1.DB4, LCM1602_IIC1.D4
  N20: LCD1.DB5, LCM1602_IIC1.D5
  N21: LCD1.DB6, LCM1602_IIC1.D6
  N22: LCD1.DB7, LCM1602_IIC1.D7
  N23: LCD1.LED+, LCM1602_IIC1.A
  N24: LCD1.LED-, LCM1602_IIC1.K
  N25: LCM1602_IIC1.LED_A, LCM1602_IIC1.LED_B
  N26: M1.pin_1, S1.M1-02, S1.M2-01
  N27: M1.pin_2, S1.M1-01, S1.M2-02
  N28: S1.IN2, S1.IN4

custom parts:
  XD-RF-5V: This is 433Mhz RF transmitter with receiver kit for Arduino ARM MCU wireless Application environment: Remote control switch, receiver module, motorcycles, automobile anti-theft products, home security products, electric doors, shutter doors, windows, remote control socket, remote control LED, remote audio remote control electric doors, garage door remote control, remote control retractable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
  FS1000A - 433Mhz RF Transmitter: This is 433Mhz RF transmitter with receiver kit for Arduino ARM MCU wireless Application environment: Remote control switch, receiver module, motorcycles, automobile anti-theft products, home security products, electric doors, shutter doors, windows, remote control socket, remote control LED, remote audio remote control electric doors, garage door remote control, remote control retractable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
  L200: ADJUSTABLE VOLTAGE AND CURRENT REGULATOR
  LCM1602 IIC: I2C-Module to use a 1602 or 2004 LCD on with the wire.h libory Serial LCD Modul
  H-Bridge with L298N: h-bridge
