# Fritzing sketch portail_na_2 (saved by Fritzing 0.9.9b)
circuit board: 8.46667cm x 5.64444cm
breadboards: 1

parts:
  Composant1 = Arduino Nano (Rev3.0)
  U1 = XD-RF-5V [package=THT]
  U2 = FS1000A - 433Mhz RF Transmitter [package=THT]
  U3 = L200 [package="pentawatt h"]
  J1 = Screw terminal - 2 pins [part_number=ALIM12V package=THT]
  J3 = Screw terminal - 2 pins [part_number=COUNTROT package=THT]
  R1 = Resistor [tolerance=±5% resistance=1k package="2010 [SMD]"]
  R2 = Resistor [tolerance=±5% resistance=680 package="2010 [SMD]"]
  R3 = Resistor [tolerance=±5% resistance=100k package="2010 [SMD]"]
  C2 = Electrolytic Capacitor [capacitance=0.1mF voltage=35V package="1010 [SMD, electrolytic]"]
  C3 = Electrolytic Capacitor [capacitance=4.7µF voltage=35V package="1010 [SMD, electrolytic]"]
  C4 = Ceramic Capacitor [capacitance=0.22mF voltage=35V package="0805 [SMD, multilayer]"]
  C5 = Ceramic Capacitor [capacitance="100 nF" voltage=35V package="0805 [SMD, multilayer]"]
  R4 = Resistor [tolerance=±5% resistance=1k package="2010 [SMD]"]
  R5 = Resistor [tolerance=±5% resistance=1k package="2010 [SMD]"]
  J2 = screw terminal, 2 pins [part_number=TRIG]
  LCM1602_IIC1 = LCM1602 IIC [part_number="LCM1602 IIC" chip_label="LCM1602 IIC" package="DIP (Dual Inline) [THT]"]
  M1 = DC Motor
  C6 = Electrolytic Capacitor [capacitance=0.1mF voltage=35V package="1010 [SMD, electrolytic]"]
  C7 = Electrolytic Capacitor [capacitance=10µF voltage=35V package="1010 [SMD, electrolytic]"]
  C8 = Ceramic Capacitor [capacitance="100 nF" voltage=35V package="0805 [SMD, multilayer]"]
  C9 = Ceramic Capacitor [capacitance=22pF voltage=35V package="0805 [SMD, multilayer]"]
  S1 = H-Bridge with L298N [part_number=ln298]
  LCD1 = LCD screen [part_number=1602A]

nets:
  GND: Composant1.GND, U1.GND, U2.GND, U3.GND, J1.pin1, J3.pin1, R2.Pin_1, C2.-, C3.-, C4.0, J2.pin1, LCM1602_IIC1.GND, C6.-, C7.+, C8.1, C9.1, S1.GND
  N1: Composant1.D2, J3.pin2, R4.Pin_0
  N2: Composant1.D3, J2.pin2
  N3: Composant1.D4, R5.Pin_0
  N4: Composant1.D5, S1.ENA, S1.ENB
  N5: Composant1.D6, S1.IN1, S1.IN3
  N6: Composant1.D7, S1.IN2, S1.IN4
  N7: Composant1.D11/MOSI, U1.DATA
  N8: Composant1.D12/MISO, U2.DATA
  VIN: Composant1.VIN, U2.VCC, U3.INPUT, J1.pin2, C2.+, C4.1
  VCC: Composant1.5V, U1.VCC, R4.Pin_1, R5.Pin_1, LCM1602_IIC1.VCC, C6.+, C7.-, C8.0, C9.0
  N9: Composant1.A7, R3.Pin_0
  N10: Composant1.A5, LCM1602_IIC1.SCL
  N11: Composant1.A4, LCM1602_IIC1.SDA
  N12: U3.LIMIT, U3.OUTPUT, R1.Pin_0, C5.0
  N13: U3.REF, C5.1
  N14: R1.Pin_1, R2.Pin_0, R3.Pin_1, C3.+
  VSS: LCM1602_IIC1.VSS, LCD1.VSS
  VDD: LCM1602_IIC1.VDD, LCD1.VDD
  N15: LCM1602_IIC1.V0, LCD1.V0
  N16: LCM1602_IIC1.RS, LCD1.RS
  N17: LCM1602_IIC1.RW, LCD1.R/W
  N18: LCM1602_IIC1.E, LCD1.E
  N19: LCM1602_IIC1.D0, LCD1.DB0
  N20: LCM1602_IIC1.D1, LCD1.DB1
  N21: LCM1602_IIC1.D2, LCD1.DB2
  N22: LCM1602_IIC1.D3, LCD1.DB3
  N23: LCM1602_IIC1.D4, LCD1.DB4
  N24: LCM1602_IIC1.D5, LCD1.DB5
  N25: LCM1602_IIC1.D6, LCD1.DB6
  N26: LCM1602_IIC1.D7, LCD1.DB7
  N27: LCM1602_IIC1.A, LCD1.LED+
  N28: LCM1602_IIC1.K, LCD1.LED-
  N29: LCM1602_IIC1.LED_A, LCM1602_IIC1.LED_B
  N30: M1.pin_1, S1.M1-02, S1.M2-01
  N31: M1.pin_2, S1.M1-01, S1.M2-02

custom parts:
  XD-RF-5V: This is 433Mhz RF transmitter with receiver kit for Arduino ARM MCU wireless Application environment: Remote control switch, receiver module, motorcycles, automobile anti-theft products, home security products, electric doors, shutter doors, windows, remote control socket, remote control LED, remote audio remote control electric doors, garage door remote control, remote control retractable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
  FS1000A - 433Mhz RF Transmitter: This is 433Mhz RF transmitter with receiver kit for Arduino ARM MCU wireless Application environment: Remote control switch, receiver module, motorcycles, automobile anti-theft products, home security products, electric doors, shutter doors, windows, remote control socket, remote control LED, remote audio remote control electric doors, garage door remote control, remote control retractable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
  L200: ADJUSTABLE VOLTAGE AND CURRENT REGULATOR
  LCM1602 IIC: I2C-Module to use a 1602 or 2004 LCD on with the wire.h libory Serial LCD Modul
  H-Bridge with L298N: h-bridge
