# Fritzing sketch portail_slave_board_0 (saved by Fritzing 0.9.9b)
circuit board: 5.32845cm x 6.60944cm
breadboards: 1

parts:
  Composant2 = Arduino Nano (Rev3.0)
  R12 = Resistor [tolerance=±5% power=0.25 resistance=1k package=THT]
  R14 = Resistor [tolerance=±5% power=0.25 resistance=10k package=THT]
  C18 = Ceramic Capacitor [capacitance="100 nF" voltage=35V package="0805 [SMD, multilayer]"]
  C19 = Ceramic Capacitor [capacitance=22pF voltage=35V package="0805 [SMD, multilayer]"]
  R15 = Resistor [tolerance=±5% power=0.25 resistance=10k package=THT]
  R16 = Resistor [tolerance=±5% power=0.25 resistance=10k package=THT]
  R17 = Resistor [tolerance=±5% power=2W resistance=1 package=THT]
  R18 = Resistor [tolerance=±5% power=0.25 resistance=1k package=THT]
  J16 = Screw terminal - 2 pins [package=THT]
  J15 = screw terminal, 2 pins
  J13 = Screw terminal - 2 pins [package=THT]
  J5 = screw terminal, 2 pins
  J14 = screw terminal, 2 pins
  C24 = Electrolytic Capacitor [capacitance=10µF voltage=35V package="100 mil [THT, electrolytic]"]
  C25 = Electrolytic Capacitor [capacitance=0.1mF voltage=35V package="100 mil [THT, electrolytic]"]
  C26 = Electrolytic Capacitor [capacitance=0.1mF voltage=35V package="100 mil [THT, electrolytic]"]
  U9 = XD-RF-5V [package=THT]

nets:
  GND: Composant2.GND, C18.1, C19.1, R17.Pin_1, J13.pin2, J5.pin2, C24.-, C25.-, C26.-, U9.GND
  N1: Composant2.D2, R12.Pin_1, J13.pin1
  N2: Composant2.D5, R14.Pin_1
  N3: Composant2.D6, R15.Pin_1
  N4: Composant2.D7, R16.Pin_1
  N5: Composant2.D11/MOSI, U9.DATA
  N6: Composant2.VIN, J5.pin1, C25.+
  5V: Composant2.5V, R12.Pin_0, C18.0, C19.0, C26.+, U9.VCC
  N7: Composant2.A7, R18.Pin_1, C24.+
  N8: R14.Pin_0, J15.pin2
  N9: R15.Pin_0, J15.pin1
  N10: R16.Pin_0, J16.pin1
  N11: R17.Pin_0, R18.Pin_0, J14.pin1

custom parts:
  XD-RF-5V: This is 433Mhz RF transmitter with receiver kit for Arduino ARM MCU wireless Application environment: Remote control switch, receiver module, motorcycles, automobile anti-theft products, home security products, electric doors, shutter doors, windows, remote control socket, remote control LED, remote audio remote control electric doors, garage door remote control, remote control retractable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
