# Fritzing sketch portail_slave_0 (saved by Fritzing 0.9.9b)
circuit board: 5.45782cm x 5.8532cm
breadboards: 1

parts:
  Composant2 = Arduino Nano (Rev3.0)
  J5 = Screw terminal - 2 pins [part_number=ALIM12V package=THT]
  C10 = Electrolytic Capacitor [capacitance=0.1mF voltage=35V package="1010 [SMD, electrolytic]"]
  C12 = Ceramic Capacitor [capacitance=0.22mF voltage=35V package="0805 [SMD, multilayer]"]
  C13 = Ceramic Capacitor [capacitance="100 nF" voltage=35V package="0805 [SMD, multilayer]"]
  U6 = L200 [package="pentawatt h"]
  R11 = Resistor [tolerance=±5% power=0.25 resistance=1k package=THT]
  R12 = Resistor [tolerance=±5% power=0.25 resistance=1k package=THT]
  R13 = Resistor [tolerance=±5% power=0.25 resistance=1k package=THT]
  R14 = Resistor [tolerance=±5% power=0.25 resistance=100k package=THT]
  R15 = Resistor [tolerance=±5% power=0.25 resistance=680 package=THT]
  LCD3 = LCD screen [part_number=1602A]
  LCM1602_IIC3 = LCM1602 IIC [part_number="LCM1602 IIC" chip_label="LCM1602 IIC" package="DIP (Dual Inline) [THT]"]
  M3 = DC Motor
  S3 = H-Bridge with L298N [part_number=ln298]
  C30 = Electrolytic Capacitor [capacitance=0.1mF voltage=35V package="100 mil [THT, electrolytic]"]
  C31 = Electrolytic Capacitor [capacitance=10µF voltage=35V package="100 mil [THT, electrolytic]"]
  S11 = Pushbutton [part_number=TRIG package=THT]
  S12 = SWITCH-MOMENTARY-2 [part_number=ROT package=reed_switch_pth]

nets:
  GND: Composant2.GND, J5.pin1, C10.-, C12.0, C13.1, U6.GND, U6.REF, R15.Pin_0, LCM1602_IIC3.GND, S3.GND, C30.-, C31.-, S11.leg0, S12.1
  N1: Composant2.D2, R12.Pin_0, S12.2
  N2: Composant2.D3, R11.Pin_0, S11.leg1
  N3: Composant2.D5, S3.ENA, S3.ENB
  N4: Composant2.D6, S3.IN1, S3.IN3
  N5: Composant2.D7, S3.IN2, S3.IN4
  N6: Composant2.VIN, J5.pin2, C10.+, C12.1, U6.INPUT
  5V: Composant2.5V, R11.Pin_1, R12.Pin_1, LCM1602_IIC3.VCC, C30.+
  N7: Composant2.A7, R14.Pin_1
  N8: Composant2.A5, LCM1602_IIC3.SCL
  N9: Composant2.A4, LCM1602_IIC3.SDA
  N10: C13.0, U6.LIMIT, U6.OUTPUT, R13.Pin_1, S3.12V
  N11: R13.Pin_0, R14.Pin_0, R15.Pin_1, C31.+
  VSS: LCD3.VSS, LCM1602_IIC3.VSS
  VDD: LCD3.VDD, LCM1602_IIC3.VDD
  N12: LCD3.V0, LCM1602_IIC3.V0
  N13: LCD3.RS, LCM1602_IIC3.RS
  N14: LCD3.R/W, LCM1602_IIC3.RW
  N15: LCD3.E, LCM1602_IIC3.E
  N16: LCD3.DB0, LCM1602_IIC3.D0
  N17: LCD3.DB1, LCM1602_IIC3.D1
  N18: LCD3.DB2, LCM1602_IIC3.D2
  N19: LCD3.DB3, LCM1602_IIC3.D3
  N20: LCD3.DB4, LCM1602_IIC3.D4
  N21: LCD3.DB5, LCM1602_IIC3.D5
  N22: LCD3.DB6, LCM1602_IIC3.D6
  N23: LCD3.DB7, LCM1602_IIC3.D7
  N24: LCD3.LED+, LCM1602_IIC3.A
  N25: LCD3.LED-, LCM1602_IIC3.K
  N26: LCM1602_IIC3.LED_A, LCM1602_IIC3.LED_B
  N27: M3.pin_1, S3.M1-02, S3.M2-01
  N28: M3.pin_2, S3.M1-01, S3.M2-02

custom parts:
  L200: ADJUSTABLE VOLTAGE AND CURRENT REGULATOR
  LCM1602 IIC: I2C-Module to use a 1602 or 2004 LCD on with the wire.h libory Serial LCD Modul
  H-Bridge with L298N: h-bridge
