# Fritzing sketch tx433_withgarage_scode (saved by Fritzing 0.9.9b)
circuit board: 5.45782cm x 5.8532cm
breadboards: 1

parts:
  Composant2 = Arduino Nano (Rev3.0)
  J5 = Screw terminal - 2 pins [part_number=ALIM12V package=THT]
  ANT2 = Antenna
  C26 = Electrolytic Capacitor [capacitance=0.1mF voltage=35V package="100 mil [THT, electrolytic]"]
  R17 = Resistor [tolerance=±5% power=0.25 resistance=2.2k package=THT]
  R18 = Resistor [tolerance=±5% power=0.25 resistance=1k package=THT]
  C29 = Electrolytic Capacitor [capacitance=0.1mF voltage=35V package="100 mil [THT, electrolytic]"]
  U9 = FS1000A - 433Mhz RF Transmitter [package=THT]
  BT1 = Bluetooth HC-06d [package=THT]
  S10 = SWITCH-MOMENTARY-2 [part_number=POC package=reed_switch_pth]

nets:
  GND: Composant2.GND, J5.pin1, C26.-, R17.Pin_1, C29.-, U9.GND, BT1.GND, S10.1
  N1: Composant2.D2, BT1.TXD
  N2: Composant2.D3, R18.Pin_0
  N3: Composant2.D4, S10.2
  N4: Composant2.D12/MISO, U9.DATA
  VIN: Composant2.VIN, J5.pin2, C26.+, U9.VCC
  5V: Composant2.5V, C29.+, BT1.VCC
  N5: ANT2.antenna_lead, U9.Antenna
  N6: R17.Pin_0, R18.Pin_1, BT1.RXD

custom parts:
  FS1000A - 433Mhz RF Transmitter: This is 433Mhz RF transmitter with receiver kit for Arduino ARM MCU wireless Application environment: Remote control switch, receiver module, motorcycles, automobile anti-theft products, home security products, electric doors, shutter doors, windows, remote control socket, remote control LED, remote audio remote control electric doors, garage door remote control, remote control retractable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
  Bluetooth HC-06d: Bluetooth HC-06 - face down, pins down 16.5mm x 37.5mm PCB
